# Fritzing sketch resistor (saved by Fritzing 0.9.3b)
breadboards: 1

parts:
  Raspberry_Pi_1 = Raspberry Pi 3 [part_number=RPI-3-V1.2]  # not connected
  R2 = PHOTOCELL [package=photocell]
  C1 = Capacitor Polarized [package=cpol-radial-10uf-25v]  # not connected

nets:
  N1: R2.P$1, R2.P$2
