# Fritzing sketch blinkuserchoice (saved by Fritzing 0.9.3b)
breadboards: 1

parts:
  LED1 = LED - 5mm [color="Red (633nm)" package="5 mm [THT]"]
  R1 = Resistor [tolerance=±2% resistance=2.0 package=THT]
  Raspberry_Pi_1 = Raspberry Pi 3 [part_number=RPI-3-V1.2]
  LED2 = LED - 5mm [color="Green (555nm)" package="5 mm [THT]"]
  R2 = Resistor [tolerance=±2% resistance=2.0 package=THT]

nets:
  N1: LED1.cathode, R1.Pin_1
  N2: LED1.anode, Raspberry_Pi_1.GPIO4
  N3: R1.Pin_0, Raspberry_Pi_1.GND, R2.Pin_0
  N4: Raspberry_Pi_1.GPIO17, LED2.anode
  N5: LED2.cathode, R2.Pin_1
