# Fritzing sketch morsecode (saved by Fritzing 0.9.3b)
breadboards: 1

parts:
  R1 = Resistor [tolerance=±2% resistance=2.0 package=THT]  # not connected
  Raspberry_Pi_1 = Raspberry Pi 3 [part_number=RPI-3-V1.2]
  J1 = Piezo Speaker

nets:
  N1: Raspberry_Pi_1.GPIO4, J1.pin2
