# Fritzing sketch pushbutton (saved by Fritzing 0.9.3b)
breadboards: 1

parts:
  Raspberry_Pi_1 = Raspberry Pi 3 [part_number=RPI-3-V1.2]
  R2 = Resistor [tolerance=±2% resistance=2.0 package=THT]
  S1 = Pushbutton [package="[THT]"]

nets:
  N1: Raspberry_Pi_1.3v3, R2.Pin_0
  N2: Raspberry_Pi_1.GND, S1.Pin_1, S1.Pin_2
  N3: R2.Pin_1, S1.Pin_3, S1.Pin_4
